// Logisim project BitClear.circ as structural Verilog: 2 circuits, main circuit main
module main (
  input  B0,
  input  B1,
  input  B2,
  output [7:0] out_4,
  output [7:0] out_5
);

  wire [7:0] not_1_out, Pri1_out_4;

  priority_encoder Pri1 (.in_1(B2), .in_2(B1), .in_3(B0), .out_4(Pri1_out_4));
  assign not_1_out = ~Pri1_out_4;  // NOT_Gate not_1, 8 bits wide
  assign out_4 = not_1_out & 8'hea;  // AND_Gate and_1, 8 bits wide

  assign out_5 = 8'hea;

  // Notes on the sheet:
  //   Rergister to set
endmodule

module priority_encoder (
  input  in_1,
  input  in_2,
  input  in_3,
  output [7:0] out_4
);

  wire not_1_out, not_2_out, not_3_out;

  not not_1 (not_1_out, in_1);
  not not_2 (not_2_out, in_2);
  not not_3 (not_3_out, in_3);
  and and_1 (out_4[0], not_3_out, not_2_out, not_1_out);
  and and_2 (out_4[1], not_3_out, not_2_out, in_1);
  and and_3 (out_4[2], not_3_out, in_2, not_1_out);
  and and_4 (out_4[3], not_3_out, in_2, in_1);
  and and_5 (out_4[4], in_3, not_2_out, not_1_out);
  and and_6 (out_4[5], in_3, not_2_out, in_1);
  and and_7 (out_4[6], in_3, in_2, not_1_out);
  and and_8 (out_4[7], in_3, in_2, in_1);
endmodule
