// Logisim project BitSet.circ as structural Verilog: 1 circuit, main circuit main
module main (
  input  B0,
  input  B1,
  input  B2,
  output [7:0] out_4,
  output [7:0] out_5,
  output [7:0] out_6
);

  wire not_1_out, not_2_out, not_3_out;

  not not_1 (not_1_out, B0);
  not not_2 (not_2_out, B1);
  not not_3 (not_3_out, B2);
  and and_1 (out_4[0], not_3_out, not_2_out, not_1_out);
  and and_2 (out_4[1], not_3_out, not_2_out, B0);
  and and_3 (out_4[2], not_3_out, B1, not_1_out);
  and and_4 (out_4[3], not_3_out, B1, B0);
  and and_5 (out_4[4], B2, not_2_out, not_1_out);
  and and_6 (out_4[5], B2, not_2_out, B0);
  and and_7 (out_4[6], B2, B1, not_1_out);
  and and_8 (out_4[7], B2, B1, B0);
  assign out_5 = out_4 | 8'h45;  // OR_Gate or_1, 8 bits wide

  assign out_6 = 8'h45;

  // Notes on the sheet:
  //   Rergister to set
endmodule
