// Logisim project CLAB_Adder.circ as structural Verilog: 4 circuits, main circuit main
module main (
  input  [7:0] A,
  input  [7:0] B,
  input  in_3,
  output [7:0] out_4
);

  wire and_11_out, and_12_out, and_13_out, and_14_out, and_15_out, and_16_out, and_17_out, and_18_out,
       and_19_out, C0, C1, C2, C3, C4, G0, G1, G2, G3, G4, P0, P1, P2, P3, P4, xor_1_out, xor_2_out,
       xor_3_out, xor_4_out, xor_5_out;

  // Probe on A
  // Probe on B
  xor xor_1 (xor_1_out, A[0], B[0]);
  xor xor_2 (xor_2_out, A[1], B[1]);
  xor xor_3 (xor_3_out, A[2], B[2]);
  xor xor_4 (xor_4_out, A[3], B[3]);
  xor xor_5 (xor_5_out, A[4], B[4]);
  and and_1 (P0, xor_1_out, in_3);
  and and_2 (G0, A[0], B[0]);
  and and_3 (P1, xor_2_out, C0);
  and and_4 (G1, A[1], B[1]);
  and and_5 (P2, xor_3_out, C1);
  and and_6 (G2, A[2], B[2]);
  and and_7 (P3, xor_4_out, C2);
  and and_8 (G3, A[3], B[3]);
  and and_9 (P4, xor_5_out, C3);
  and and_10 (G4, A[4], B[4]);
  xor xor_6 (out_4[0], xor_1_out, in_3);
  xor xor_7 (out_4[1], xor_2_out, C0);
  xor xor_8 (out_4[2], xor_3_out, C1);
  xor xor_9 (out_4[3], xor_4_out, C2);
  xor xor_10 (out_4[4], xor_5_out, C3);
  // Probe on out_4
  LED led_1 (.in(C4));
  and and_11 (and_11_out, in_3, P0, P1, P2, P3);
  and and_12 (and_12_out, G0, P3, P1, P2);
  and and_13 (and_13_out, G1, P2, P3);
  and and_14 (and_14_out, G2, P3);
  and and_15 (and_15_out, G0, P1, P2, P3, P4, in_3);
  and and_16 (and_16_out, G0, P1, P2, P3, P4);
  and and_17 (and_17_out, G1, P2, P3, P4);
  and and_18 (and_18_out, G2, P3, P4);
  and and_19 (and_19_out, G3, P4);
  or or_1 (C3, and_11_out, and_12_out, and_13_out, and_14_out, G3);
  or or_2 (C4, and_15_out, and_16_out, and_18_out, and_19_out, G4);
  Carry0 carry0_1 (.in_1(in_3), .in_2(P0), .in_3(G0), .out_4(C0));
  Carry1 carry1_1 (.in_1(in_3), .in_2(P0), .in_3(P1), .in_4(P1), .in_5(G0), .in_6(G1), .out_7(C1));
  Carry2 carry2_1 (
    .in_1(in_3), .in_2(P0), .in_3(P1), .in_4(P2), .in_5(G0), .in_6(P1), .in_7(P2), .in_8(G1), .in_9(P2),
    .in_10(G2), .out_11(C2));

  // Other names for the same wires on the sheet: Cin = in_3; S0 = out_4[0]; S1 = out_4[1]; S2 = out_4[2];
  //   S3 = out_4[3]; S4 = out_4[4]

  // Notes on the sheet:
  //   C3 =G3+G2*P3+P3*P2G1+ P3*P2*P1*G0+P3*P2*P1*P0*Cin
  //   C4 =G4+G3*P4+P4*P3*G2+ P4*P3*P2*G1+P4*P3*P2*P1*P1*G0*P4*P3*P2*P1*P0*Cin
  //   C0 =G0+P0*Cin
  //   C1 =G1+P1*G0+ P1*P0*Cin
endmodule

module Carry0 (
  input  in_1,
  input  in_2,
  input  in_3,
  output out_4
);

  wire and_1_out;

  and and_1 (and_1_out, in_1, in_2);
  or or_1 (out_4, and_1_out, in_3);

  // Notes on the sheet:
  //   C0 =G0+P0*Cin
endmodule

module Carry1 (
  input  in_1,
  input  in_2,
  input  in_3,
  input  in_4,
  input  in_5,
  input  in_6,
  output out_7
);

  wire and_1_out, and_2_out;

  and and_1 (and_1_out, in_1, in_2, in_3);
  and and_2 (and_2_out, in_4, in_5);
  or or_1 (out_7, and_1_out, and_2_out, in_6);

  // Notes on the sheet:
  //   C1 =G1+P1*G0+ P1*P0*Cin
endmodule

module Carry2 (
  input  in_1,
  input  in_2,
  input  in_3,
  input  in_4,
  input  in_5,
  input  in_6,
  input  in_7,
  input  in_8,
  input  in_9,
  input  in_10,
  output out_11
);

  wire and_1_out, and_2_out, and_3_out;

  and and_1 (and_1_out, in_1, in_2, in_3, in_4);
  and and_2 (and_2_out, in_5, in_6, in_7);
  and and_3 (and_3_out, in_8, in_9);
  or or_1 (out_11, and_1_out, and_2_out, and_3_out, in_10);

  // Notes on the sheet:
  //   C2 =G2+G1*P2+P2*P1*G0+ P2*P1*P0*Cin
endmodule
