// Logisim project ShiftBit.circ as structural Verilog: 2 circuits, main circuit main
module main (
  input  [2:0] in_1,
  input  in_2,
  output [2:0] out_3,
  output [2:0] out_4
);

  Unit_Shift unit_shift_1 (.in_1(in_1), .in_2(in_2), .out_3(out_3));
  Unit_Shift unit_shift_2 (.in_1(out_3), .in_2(in_2), .out_3(out_4));
endmodule

module Unit_Shift (
  input  [2:0] in_1,
  input  in_2,
  output [2:0] out_3
);

  wire and_2_out, and_3_out, not_1_out;

  not not_1 (not_1_out, in_2);
  and and_1 (out_3[0], in_2, in_1[1]);
  and and_2 (and_2_out, in_2, in_1[2]);
  and and_3 (and_3_out, not_1_out, in_1[0]);
  and and_4 (out_3[2], not_1_out, in_1[1]);
  or or_1 (out_3[1], and_2_out, and_3_out);
endmodule
