// Logisim project adders.circ as structural Verilog: 1 circuit, main circuit main
module main (
  input  [7:0] A,
  input  [7:0] B,
  input  in_3,
  output Sum,
  output Carry,
  output Sum_2,
  output Carry_2
);

  wire and_2_out, and_3_out, xor_2_out;

  xor xor_1 (Sum, A[0], B[0]);
  and and_1 (Carry, A[0], B[0]);
  xor xor_2 (xor_2_out, A[0], B[0]);
  and and_2 (and_2_out, xor_2_out, in_3);
  and and_3 (and_3_out, A[0], B[0]);
  xor xor_3 (Sum_2, xor_2_out, in_3);
  or or_1 (Carry_2, and_2_out, and_3_out);

  // Other names for the same wires on the sheet: Cin = in_3
endmodule
