// Logisim project ripple_carry.circ as structural Verilog: 1 circuit, main circuit main
module main (
  input  [7:0] A,
  input  [7:0] B,
  input  in_3,
  output [7:0] out_4,
  output out_5,
  output out_6,
  output out_7,
  output out_8,
  output out_9,
  output out_10,
  output out_11,
  output out_12
);

  wire and_1_out, and_2_out, and_3_out, and_4_out, and_5_out, and_6_out, and_7_out, and_8_out, and_9_out,
       and_10_out, and_11_out, and_12_out, and_13_out, and_14_out, and_15_out, and_16_out, C1, C2, C3, C4,
       C5, C6, C7, Cout, xor_1_out, xor_2_out, xor_3_out, xor_4_out, xor_5_out, xor_6_out, xor_7_out,
       xor_8_out;

  // Probe on A
  // Probe on B
  xor xor_1 (xor_1_out, A[0], B[0]);
  xor xor_2 (xor_2_out, A[1], B[1]);
  xor xor_3 (xor_3_out, A[2], B[2]);
  xor xor_4 (xor_4_out, A[3], B[3]);
  xor xor_5 (xor_5_out, A[4], B[4]);
  xor xor_6 (xor_6_out, A[5], B[5]);
  xor xor_7 (xor_7_out, A[6], B[6]);
  xor xor_8 (xor_8_out, A[7], B[7]);
  and and_1 (and_1_out, xor_1_out, in_3);
  and and_2 (and_2_out, A[0], B[0]);
  and and_3 (and_3_out, xor_2_out, C1);
  and and_4 (and_4_out, A[1], B[1]);
  and and_5 (and_5_out, xor_3_out, C2);
  and and_6 (and_6_out, A[2], B[2]);
  and and_7 (and_7_out, xor_4_out, C3);
  and and_8 (and_8_out, A[3], B[3]);
  and and_9 (and_9_out, xor_5_out, C4);
  and and_10 (and_10_out, A[4], B[4]);
  and and_11 (and_11_out, xor_6_out, C5);
  and and_12 (and_12_out, A[5], B[5]);
  and and_13 (and_13_out, xor_7_out, C6);
  and and_14 (and_14_out, A[6], B[6]);
  and and_15 (and_15_out, xor_8_out, C7);
  and and_16 (and_16_out, A[7], B[7]);
  xor xor_9 (out_4[0], xor_1_out, in_3);
  or or_1 (C1, and_1_out, and_2_out);
  xor xor_10 (out_4[1], xor_2_out, C1);
  or or_2 (C2, and_3_out, and_4_out);
  xor xor_11 (out_4[2], xor_3_out, C2);
  or or_3 (C3, and_5_out, and_6_out);
  xor xor_12 (out_4[3], xor_4_out, C3);
  or or_4 (C4, and_7_out, and_8_out);
  xor xor_13 (out_4[4], xor_5_out, C4);
  or or_5 (C5, and_9_out, and_10_out);
  xor xor_14 (out_4[5], xor_6_out, C5);
  or or_6 (C6, and_11_out, and_12_out);
  xor xor_15 (out_4[6], xor_7_out, C6);
  or or_7 (C7, and_13_out, and_14_out);
  xor xor_16 (out_4[7], xor_8_out, C7);
  or or_8 (Cout, and_15_out, and_16_out);
  // Probe on out_4
  LED led_1 (.in(Cout));

  assign out_5 = out_4[0];
  assign out_6 = out_4[1];
  assign out_7 = out_4[2];
  assign out_8 = out_4[3];
  assign out_9 = out_4[4];
  assign out_10 = out_4[5];
  assign out_11 = out_4[6];
  assign out_12 = out_4[7];

  // Other names for the same wires on the sheet: Cin = in_3
endmodule
