// Logisim project TwoComplementLogiSim.circ as structural Verilog: 1 circuit, main circuit main
module main (
  input  LSB,
  input  in_2,
  input  in_3,
  input  in_4,
  input  in_5,
  input  in_6,
  input  in_7,
  input  MSB,
  input  in_9
);

  wire [7:0] adder_1_out, multiplexer_1_out, not_1_out;

  // Probe on {MSB, in_7, in_6, in_5, in_4, in_3, in_2, LSB}
  assign not_1_out = ~{MSB, in_7, in_6, in_5, in_4, in_3, in_2, LSB};  // NOT_Gate not_1, 8 bits wide
  // Probe on adder_1_out
  // Probe on not_1_out
  Adder adder_1 (.a(not_1_out), .b(8'h1), .out(adder_1_out), .cin(1'b0));  // open: cout
  Multiplexer #(.width(8), .enable("false")) multiplexer_1 (
    .in0(adder_1_out), .in1({MSB, in_7, in_6, in_5, in_4, in_3, in_2, LSB}), .out(multiplexer_1_out),
    .sel(in_9));
  // Probe on multiplexer_1_out
  LED led_1 (.in(multiplexer_1_out[0]));
  LED led_2 (.in(multiplexer_1_out[1]));
  LED led_3 (.in(multiplexer_1_out[2]));
  LED led_4 (.in(multiplexer_1_out[3]));
  LED led_5 (.in(multiplexer_1_out[4]));
  LED led_6 (.in(multiplexer_1_out[5]));
  LED led_7 (.in(multiplexer_1_out[6]));
  LED led_8 (.in(multiplexer_1_out[7]));

  // Notes on the sheet:
  //   LSB
  //   MSB
endmodule
