// Logisim project FirFilter.circ as structural Verilog: 1 circuit, main circuit main
module main (
  input  in_1,
  input  in_2,
  output [7:0] Output,
  output [7:0] out_4,
  output [7:0] out_5,
  output [7:0] out_6,
  output [7:0] out_7,
  output [7:0] out_8,
  output [7:0] out_9,
  output [7:0] Input,
  output [7:0] out_11,
  output [7:0] out_12,
  output [7:0] out_13,
  output [7:0] out_14
);

  wire clock_1_out;
  wire [7:0] adder_1_out;

  ROM rom_1 (.addr(out_14), .data(Input));
  Clock clock_1 (.out(clock_1_out));
  Multiplier multiplier_1 (.a(8'h1), .b(Input), .out(out_6));  // open: cin, cout
  Register register_1 (.D(Input), .en(in_1), .clk(clock_1_out), .Q(out_11), .clr(in_2));
  Register register_2 (.D(adder_1_out), .en(in_1), .clk(clock_1_out), .Q(out_14), .clr(in_2));
  Adder adder_1 (.a(out_14), .b(8'h1), .out(adder_1_out));  // open: cin, cout
  Adder adder_2 (.a(out_6), .b(out_7), .out(out_5));  // open: cin, cout
  Multiplier multiplier_2 (.a(8'h2), .b(out_11), .out(out_7));  // open: cin, cout
  Register register_3 (.D(out_11), .en(in_1), .clk(clock_1_out), .Q(out_12), .clr(in_2));
  Multiplier multiplier_3 (.a(8'h3), .b(out_12), .out(out_8));  // open: cin, cout
  Adder adder_3 (.a(out_5), .b(out_4), .out(Output));  // open: cin, cout
  Register register_4 (.D(out_12), .en(in_1), .clk(clock_1_out), .Q(out_13), .clr(in_2));
  Multiplier multiplier_4 (.a(8'h4), .b(out_13), .out(out_9));  // open: cin, cout
  Adder adder_4 (.a(out_8), .b(out_9), .out(out_4));  // open: cin, cout

  // Notes on the sheet:
  //   contents of rom_1 (hex, n*v repeats v):
  //   2 3 5 4 6 a c 8
endmodule
