// Logisim project MemoriesRAM.circ as structural Verilog: 1 circuit, main circuit main
module main (
  input  RST,
  input  LOAD,
  input  EN,
  input  [7:0] in_4,
  input  WE,
  input  OEN,
  input  [7:0] WDATA,
  output [7:0] RDATA
);

  wire clock_1_out;
  wire [7:0] counter_1_q;

  Clock clock_1 (.out(clock_1_out));
  Counter counter_1 (
    .clr(RST), .load(LOAD), .up(1'b1), .count(EN), .clk(clock_1_out), .D(in_4), .Q(counter_1_q));  // open: carry
  RAM ram_1 (.addr(counter_1_q), .we(WE), .oe(OEN), .clk(clock_1_out), .data(RDATA));
  assign RDATA = WE ? WDATA : 8'bz;  // Controlled_Buffer controlled_buffer_1
endmodule
