// Logisim project MemoriesROM.circ as structural Verilog: 1 circuit, main circuit main
module main (
  input  in_1,
  output [7:0] out_2
);

  wire clock_1_out, d_ff_1_qn, d_ff_2_qn, d_ff_3_qn, d_ff_4_qn, d_ff_5_qn, d_ff_6_qn, d_ff_7_qn, d_ff_8_qn;
  wire [7:0] d_ff_1_q;

  Clock clock_1 (.out(clock_1_out));
  D_Flip_Flop d_ff_1 (.D(d_ff_1_qn), .clk(clock_1_out), .Q(d_ff_1_q[0]), .Qn(d_ff_1_qn));  // open: preset, reset
  D_Flip_Flop d_ff_2 (.D(d_ff_2_qn), .clk(d_ff_1_qn), .Q(d_ff_1_q[1]), .Qn(d_ff_2_qn), .reset(in_1));  // open: preset
  D_Flip_Flop d_ff_3 (.D(d_ff_3_qn), .clk(d_ff_2_qn), .Q(d_ff_1_q[2]), .Qn(d_ff_3_qn), .reset(in_1));  // open: preset
  D_Flip_Flop d_ff_4 (.D(d_ff_4_qn), .clk(d_ff_3_qn), .Q(d_ff_1_q[3]), .Qn(d_ff_4_qn), .reset(in_1));  // open: preset
  ROM rom_1 (.addr(d_ff_1_q), .data(out_2));
  D_Flip_Flop d_ff_5 (.D(d_ff_5_qn), .clk(d_ff_4_qn), .Q(d_ff_1_q[4]), .Qn(d_ff_5_qn), .reset(in_1));  // open: preset
  D_Flip_Flop d_ff_6 (.D(d_ff_6_qn), .clk(d_ff_5_qn), .Q(d_ff_1_q[5]), .Qn(d_ff_6_qn), .reset(in_1));  // open: preset
  D_Flip_Flop d_ff_7 (.D(d_ff_7_qn), .clk(d_ff_6_qn), .Q(d_ff_1_q[6]), .Qn(d_ff_7_qn), .reset(in_1));  // open: preset
  D_Flip_Flop d_ff_8 (.D(d_ff_8_qn), .clk(d_ff_7_qn), .Q(d_ff_1_q[7]), .Qn(d_ff_8_qn), .reset(in_1));  // open: preset

  // Notes on the sheet:
  //   contents of rom_1 (hex, n*v repeats v):
  //   a 70 d f c 1 13 16 21 2c 37 42 4d
endmodule
