// Logisim project SemaphoreControler_v2.circ as structural Verilog: 5 circuits, main circuit main
// S0
module main (
  input  in_1,
  output [1:0] out_2
);

  wire clock_1_out, enable_logic_1_out_3;
  wire [1:0] fsm_logic_1_out_2;
  wire [2:0] E, N;
  wire [5:0] cnt1_1_out_3;

  Clock clock_1 (.out(clock_1_out));
  LED led_1 (.in(E[0]));
  LED led_2 (.in(E[1]));
  LED led_3 (.in(E[2]));
  FSM_Logic fsm_logic_1 (.in_1(out_2), .out_2(fsm_logic_1_out_2));
  LED led_4 (.in(N[0]));
  LED led_5 (.in(N[1]));
  LED led_6 (.in(N[2]));
  LED led_7 (.in(N[0]));
  LED led_8 (.in(N[1]));
  LED led_9 (.in(N[2]));
  Register #(.width(2)) register_1 (
    .D(fsm_logic_1_out_2), .en(enable_logic_1_out_3), .clk(clock_1_out), .Q(out_2), .clr(in_1));
  Cnt1 cnt1_1 (.in_1(clock_1_out), .in_2(in_1), .out_3(cnt1_1_out_3));
  LED led_10 (.in(E[0]));
  LED led_11 (.in(E[1]));
  LED led_12 (.in(E[2]));
  Output_Logic output_logic_1 (.in_1(out_2), .out_2(N), .out_3(E));
  Enable_Logic enable_logic_1 (.in_1(cnt1_1_out_3), .in_2(out_2[0]), .out_3(enable_logic_1_out_3));

  // Other names for the same wires on the sheet: S0 = out_2[0]; S[2:0] = N; W[2:0] = E
endmodule

module Output_Logic (
  input  [1:0] in_1,
  output [2:0] out_2,
  output [2:0] out_3
);

  wire not_2_out;

  not not_1 (out_2[0], in_1[1]);
  not not_2 (not_2_out, in_1[0]);
  and and_1 (out_2[2], not_2_out, in_1[1]);
  and and_2 (out_3[2], out_2[0], not_2_out);

  assign out_2[1] = in_1[0];
  assign out_3[1:0] = {in_1[0], in_1[1]};

  // Other names for the same wires on the sheet: S1 = in_1[1]; S0 = in_1[0]
endmodule

module Cnt1 (
  input  in_1,
  input  in_2,
  output [5:0] out_3
);

  wire d_ff_1_qn, d_ff_2_qn, d_ff_3_qn, d_ff_4_qn, d_ff_5_qn, d_ff_6_qn;

  D_Flip_Flop d_ff_1 (.D(d_ff_1_qn), .clk(in_1), .Q(out_3[0]), .Qn(d_ff_1_qn), .reset(in_2));  // open: preset
  D_Flip_Flop d_ff_2 (.D(d_ff_2_qn), .clk(d_ff_1_qn), .Q(out_3[1]), .Qn(d_ff_2_qn), .reset(in_2));  // open: preset
  D_Flip_Flop d_ff_3 (.D(d_ff_3_qn), .clk(d_ff_2_qn), .Q(out_3[2]), .Qn(d_ff_3_qn), .reset(in_2));  // open: preset
  D_Flip_Flop d_ff_4 (.D(d_ff_4_qn), .clk(d_ff_3_qn), .Q(out_3[3]), .Qn(d_ff_4_qn), .reset(in_2));  // open: preset
  D_Flip_Flop d_ff_5 (.D(d_ff_5_qn), .clk(d_ff_4_qn), .Q(out_3[4]), .Qn(d_ff_5_qn), .reset(in_2));  // open: preset
  D_Flip_Flop d_ff_6 (.D(d_ff_6_qn), .clk(d_ff_5_qn), .Q(out_3[5]), .Qn(d_ff_6_qn), .reset(in_2));  // open: preset

  // Other names for the same wires on the sheet: C0 = out_3[0]; C1 = out_3[1]; C2 = out_3[2]; C3 = out_3[3];
  //   C4 = out_3[4]; C5 = out_3[5]
endmodule

module Enable_Logic (
  input  [5:0] in_1,
  input  in_2,
  output out_3
);

  wire and_1_out, and_2_out;

  and and_1 (and_1_out, in_1[5], in_1[4], in_1[3], in_1[2], in_1[1], in_1[0]);
  and and_2 (and_2_out, in_1[1], in_1[2], in_1[0]);
  Multiplexer #(.enable("false")) multiplexer_1 (.in0(and_1_out), .in1(and_2_out), .out(out_3), .sel(in_2));

  // Other names for the same wires on the sheet: C0 = in_1[0]; C1 = in_1[1]; C2 = in_1[2]; C3 = in_1[3]; C4 = in_1[4];
  //   C5 = in_1[5]; S0 = in_2
endmodule

module FSM_Logic (
  input  [1:0] in_1,
  output [1:0] out_2
);

  Adder #(.width(2)) adder_1 (.a(in_1), .b(2'b01), .out(out_2));  // open: cin, cout
endmodule
