// Logisim project Sreg.circ as structural Verilog: 1 circuit, main circuit main
module main (
  input  in_1,
  input  in_2,
  output out_3,
  output out_4,
  output out_5,
  output out_6,
  output out_7,
  output out_8,
  output out_9,
  output out_10
);

  wire clock_1_out;

  Clock clock_1 (.out(clock_1_out));
  D_Flip_Flop d_ff_1 (.D(in_1), .clk(clock_1_out), .Q(out_3), .reset(in_2));  // open: Qn, preset
  D_Flip_Flop d_ff_2 (.D(out_3), .clk(clock_1_out), .Q(out_4), .reset(in_2));  // open: Qn, preset
  D_Flip_Flop d_ff_3 (.D(out_4), .clk(clock_1_out), .Q(out_5), .reset(in_2));  // open: Qn, preset
  D_Flip_Flop d_ff_4 (.D(out_5), .clk(clock_1_out), .Q(out_6), .reset(in_2));  // open: Qn, preset
  D_Flip_Flop d_ff_5 (.D(out_6), .clk(clock_1_out), .Q(out_7), .reset(in_2));  // open: Qn, preset
  D_Flip_Flop d_ff_6 (.D(out_7), .clk(clock_1_out), .Q(out_8), .reset(in_2));  // open: Qn, preset
  D_Flip_Flop d_ff_7 (.D(out_8), .clk(clock_1_out), .Q(out_9), .reset(in_2));  // open: Qn, preset
  D_Flip_Flop d_ff_8 (.D(out_9), .clk(clock_1_out), .Q(out_10), .reset(in_2));  // open: Qn, preset
endmodule
