// Logisim project StringMachine.circ as structural Verilog: 1 circuit, main circuit main
module main (
  input  in_1,
  input  in_2,
  output [7:0] out_3,
  output [7:0] out_4
);

  wire and_1_out, and_2_out, and_3_out, and_4_out, and_5_out, and_6_out, and_7_out, and_8_out, and_9_out,
       and_10_out, and_11_out, and_12_out, and_13_out, and_14_out, and_15_out, and_16_out, clock_1_out,
       multiplexer_1_out, not_1_out, not_2_out, not_3_out, not_4_out, not_5_out, not_6_out, not_7_out,
       not_8_out, not_9_out, not_10_out;
  wire [1:0] or_2_out;
  wire [2:0] or_5_out, register_2_q;
  wire [7:0] adder_1_out;

  ROM rom_1 (.addr(out_4), .data(out_3));
  not not_1 (not_1_out, out_3[7]);
  not not_2 (not_2_out, out_3[4]);
  not not_3 (not_3_out, out_3[5]);
  not not_4 (not_4_out, out_3[2]);
  not not_5 (not_5_out, out_3[3]);
  Clock clock_1 (.out(clock_1_out));
  not not_6 (not_6_out, out_3[1]);
  not not_7 (not_7_out, out_3[0]);
  not not_8 (not_8_out, register_2_q[0]);
  not not_9 (not_9_out, register_2_q[1]);
  not not_10 (not_10_out, register_2_q[2]);
  and and_1 (and_1_out, not_1_out, out_3[6], not_3_out, not_2_out, out_3[3], out_3[2], not_6_out, out_3[0]);
  and and_2 (and_2_out, not_1_out, out_3[6], out_3[5], not_2_out, out_3[3], out_3[2], out_3[1], out_3[0]);
  and and_3 (and_3_out, not_1_out, out_3[6], out_3[5], out_3[4], not_5_out, not_4_out, out_3[1], not_7_out);
  and and_4 (and_4_out, not_1_out, out_3[6], out_3[5], not_2_out, not_5_out, out_3[2], not_6_out, out_3[0]);
  Adder adder_1 (.a(out_4), .b(8'h1), .out(adder_1_out));  // open: cin, cout
  and and_5 (and_5_out, register_2_q[2], not_8_out);
  and and_6 (and_6_out, register_2_q[0], register_2_q[1]);
  or or_1 (or_2_out[1], and_6_out, and_5_out);
  Multiplexer #(.select(2), .enable("false")) multiplexer_1 (
    .in0(and_1_out), .in1(and_2_out), .in2(and_3_out), .in3(and_4_out), .out(multiplexer_1_out),
    .sel(or_2_out));
  Register register_1 (.D(adder_1_out), .en(in_1), .clk(clock_1_out), .Q(out_4), .clr(in_2));
  and and_7 (and_7_out, not_10_out, not_9_out, register_2_q[0]);
  and and_8 (and_8_out, register_2_q[1], not_8_out);
  or or_2 (or_2_out[0], and_7_out, and_8_out, and_9_out);
  and and_9 (and_9_out, register_2_q[2], not_8_out);
  and and_10 (and_10_out, not_8_out, register_2_q[2], multiplexer_1_out);
  or or_3 (or_5_out[2], and_10_out, and_11_out);
  and and_11 (and_11_out, register_2_q[0], register_2_q[1], multiplexer_1_out);
  and and_12 (and_12_out, register_2_q[0], not_10_out, not_9_out, multiplexer_1_out);
  and and_13 (and_13_out, not_8_out, multiplexer_1_out);
  and and_14 (and_14_out, not_8_out, register_2_q[1], multiplexer_1_out);
  or or_4 (or_5_out[1], and_12_out, and_14_out);
  and and_15 (and_15_out, register_2_q[2], multiplexer_1_out);
  or or_5 (or_5_out[0], and_13_out, and_15_out);
  Register #(.width(3)) register_2 (.D(or_5_out), .en(in_1), .clk(clock_1_out), .Q(register_2_q), .clr(in_2));
  and and_16 (and_16_out, register_2_q[0], register_2_q[2]);
  LED led_1 (.in(and_16_out));

  // Notes on the sheet:
  //   contents of rom_1 (hex, n*v repeats v):
  //   54 68 69 73 20 69 73 20 20 4d 6f 6f 72 65 20 6d 61 63 68 69 6e 65
  //   Input
endmodule
