// Logisim project BusDriver.circ as structural Verilog: 1 circuit, main circuit main
module main (
  input  Control_signal
);

  wire not_1_out;
  wire [7:0] controlled_buffer_1_out;

  not not_1 (not_1_out, Control_signal);
  assign controlled_buffer_1_out = Control_signal ? 8'h10 : 8'bz;  // Controlled_Buffer controlled_buffer_1
  LED led_1 (.in(Control_signal));
  assign controlled_buffer_1_out = not_1_out ? 8'h1 : 8'bz;  // Controlled_Buffer controlled_buffer_2
  LED led_2 (.in(not_1_out));
  // Probe on controlled_buffer_1_out
  // Probe on controlled_buffer_1_out

  // Notes on the sheet:
  //   Data signals
  //   Tri state buffer
  //   8 bit bus 
endmodule
