// Logisim project HelloLed.circ as structural Verilog: 5 circuits, main circuit main
// S0
module main (
  input  in_1,
  input  in_2
);

  wire C1, C2, C3, C4, clock_1_out, not_1_out, not_2_out;
  wire [3:0] adder_1_out, register_1_q;
  wire [7:0] register_2_q, register_3_q, register_4_q, register_5_q, rom_1_data;

  not not_1 (not_1_out, register_1_q[0]);
  not not_2 (not_2_out, register_1_q[1]);
  Clock clock_1 (.out(clock_1_out));
  ROM #(.addrWidth(4)) rom_1 (.addr(register_1_q), .data(rom_1_data));
  and and_1 (C1, not_1_out, not_2_out);
  and and_2 (C2, register_1_q[0], not_2_out);
  and and_3 (C3, not_1_out, register_1_q[1]);
  and and_4 (C4, register_1_q[0], register_1_q[1]);
  Adder #(.width(4)) adder_1 (.a(register_1_q), .b(4'b0001), .out(adder_1_out));  // open: cin, cout
  Register #(.width(4)) register_1 (.D(adder_1_out), .en(in_1), .clk(clock_1_out), .Q(register_1_q), .clr(in_2));
  Register register_2 (.D(rom_1_data), .en(C1), .clk(clock_1_out), .Q(register_2_q), .clr(in_2));
  Register register_3 (.D(rom_1_data), .en(C2), .clk(clock_1_out), .Q(register_3_q), .clr(in_2));
  Register register_4 (.D(rom_1_data), .en(C3), .clk(clock_1_out), .Q(register_4_q), .clr(in_2));
  Register register_5 (.D(rom_1_data), .en(C4), .clk(clock_1_out), .Q(register_5_q), .clr(in_2));
  DotMatrix #(.matrixcols(4), .matrixrows(5)) dotmatrix_1 (
    .col0(register_2_q[4:0]), .col1(register_3_q[4:0]), .col2(register_4_q[4:0]), .col3(register_5_q[4:0]));

  // Notes on the sheet:
  //   contents of rom_1 (hex, n*v repeats v):
  //   1f 4 4 1f e 11 11 e 1f 1 1 1 f 12 12 f
endmodule

module Output_Logic (
  input  [1:0] in_1,
  output [2:0] out_2,
  output [2:0] out_3
);

  wire not_2_out;

  not not_1 (out_2[0], in_1[1]);
  not not_2 (not_2_out, in_1[0]);
  and and_1 (out_2[2], not_2_out, in_1[1]);
  and and_2 (out_3[2], out_2[0], not_2_out);

  assign out_2[1] = in_1[0];
  assign out_3[1:0] = {in_1[0], in_1[1]};

  // Other names for the same wires on the sheet: S1 = in_1[1]; S0 = in_1[0]
endmodule

module Cnt1 (
  input  in_1,
  input  in_2,
  output [5:0] out_3
);

  wire d_ff_1_qn, d_ff_2_qn, d_ff_3_qn, d_ff_4_qn, d_ff_5_qn, d_ff_6_qn;

  D_Flip_Flop d_ff_1 (.D(d_ff_1_qn), .clk(in_1), .Q(out_3[0]), .Qn(d_ff_1_qn), .reset(in_2));  // open: preset
  D_Flip_Flop d_ff_2 (.D(d_ff_2_qn), .clk(d_ff_1_qn), .Q(out_3[1]), .Qn(d_ff_2_qn), .reset(in_2));  // open: preset
  D_Flip_Flop d_ff_3 (.D(d_ff_3_qn), .clk(d_ff_2_qn), .Q(out_3[2]), .Qn(d_ff_3_qn), .reset(in_2));  // open: preset
  D_Flip_Flop d_ff_4 (.D(d_ff_4_qn), .clk(d_ff_3_qn), .Q(out_3[3]), .Qn(d_ff_4_qn), .reset(in_2));  // open: preset
  D_Flip_Flop d_ff_5 (.D(d_ff_5_qn), .clk(d_ff_4_qn), .Q(out_3[4]), .Qn(d_ff_5_qn), .reset(in_2));  // open: preset
  D_Flip_Flop d_ff_6 (.D(d_ff_6_qn), .clk(d_ff_5_qn), .Q(out_3[5]), .Qn(d_ff_6_qn), .reset(in_2));  // open: preset

  // Other names for the same wires on the sheet: C0 = out_3[0]; C1 = out_3[1]; C2 = out_3[2]; C3 = out_3[3];
  //   C4 = out_3[4]; C5 = out_3[5]
endmodule

module Enable_Logic (
  input  [5:0] in_1,
  input  in_2,
  output out_3
);

  wire and_1_out, and_2_out;

  and and_1 (and_1_out, in_1[5], in_1[4], in_1[3], in_1[2], in_1[1], in_1[0]);
  and and_2 (and_2_out, in_1[1], in_1[2], in_1[0]);
  Multiplexer #(.enable("false")) multiplexer_1 (.in0(and_1_out), .in1(and_2_out), .out(out_3), .sel(in_2));

  // Other names for the same wires on the sheet: C0 = in_1[0]; C1 = in_1[1]; C2 = in_1[2]; C3 = in_1[3]; C4 = in_1[4];
  //   C5 = in_1[5]; S0 = in_2
endmodule

module FSM_Logic (
  input  [3:0] in_1,
  output [3:0] out_2
);

  Adder #(.width(4)) adder_1 (.a(in_1), .b(4'b0001), .out(out_2));  // open: cin, cout
endmodule
